# Fritzing sketch rc_dimmer_arduino (saved by Fritzing 0.9.3b)
breadboards: 1

parts:
  Arduino_UNO = Arduino Uno (Rev3) - ICSP
  U1 = TRIAC [package=to-92]
  SP1 = SPEAKER [package=pcb_mount_speaker]
  U2 = Optocoupler [package=THT]
  part = Diode [package=diode-hv]
  part_2 = Diode [package=diode-hv]
  part_3 = Diode [package=diode-hv]
  part_4 = Diode [package=diode-hv]
  R1 = Resistor [tolerance=±5% resistance=20k package=THT]
  R2 = Resistor [tolerance=±5% resistance=20k package=THT]
  R3 = Resistor [tolerance=±5% resistance=20k package=THT]
  U3 = MOC3031-M [package=dil06]
  R4 = Resistor [tolerance=±5% resistance=1k package=THT]
  V1 = AC Power [voltage=230 frequency=60]
  C2 = Capacitor [part_number="103J 0.01uf" package=cap-pth-small-kit]
  R5 = Resistor [tolerance=±5% resistance=100 package=THT]
  IR1 = TSOP312.., 314.. [package=THT]
  LOAD = Incandescent light bulb small [package="bulb sm"]

nets:
  N1: Arduino_UNO.D8, SP1.+
  GND: Arduino_UNO.GND, SP1.-, U2.Pin_4, U3.2, IR1.GND
  N2: Arduino_UNO.D2, U2.Pin_5, R3.Pin_1
  N3: Arduino_UNO.D4, IR1.Data
  N4: Arduino_UNO.D5_PWM, U3.1
  N5: Arduino_UNO.5V, R3.Pin_0, IR1.Vs
  N6: U1.M1, C2.2, LOAD.1
  N7: U1.G, U3.4
  N8: U1.M2, R4.Pin_1
  N9: U2.Pin_1, part.A, part_2.A
  N10: U2.Pin_2, part_4.C
  N11: part_2.C, part_3.A, R1.Pin_0
  N12: part_4.A, R2.Pin_0
  GND_2: R1.Pin_1, V1.V-, LOAD.2
  N13: R2.Pin_1, V1.V+, R5.Pin_1
  N14: U3.6, R4.Pin_0
  N15: C2.1, R5.Pin_0

notes:
  Arduino GND
  +
  -
  Optocoupler
  Optotriac
  AC Mains
  Neutral
  FBR
  Infrarred Receiver

custom parts:
  MOC3031-M: Opto-isolated TRIAC
